// Logisim project clock.circ as structural Verilog: 2 circuits, main circuit main
module main (
);

  wire clock_1_out, flip_flop_1_nq, flip_flop_1_q, flip_flop_2_nq, flip_flop_2_q, flip_flop_3_nq,
       flip_flop_3_q, not_1_out, undriven, undriven_2;

  Clock clock_1 (.out(clock_1_out));
  not not_1 (not_1_out, clock_1_out);
  flip_flop flip_flop_1 (
    .SRST(undriven), .ARST(undriven_2), .nCLK(not_1_out), .CLK(clock_1_out), .Q(flip_flop_1_q),
    .nQ(flip_flop_1_nq));
  flip_flop flip_flop_2 (
    .SRST(undriven), .ARST(undriven_2), .nCLK(flip_flop_1_q), .CLK(flip_flop_1_nq), .Q(flip_flop_2_q),
    .nQ(flip_flop_2_nq));
  flip_flop flip_flop_3 (
    .SRST(undriven), .ARST(undriven_2), .nCLK(flip_flop_2_q), .CLK(flip_flop_2_nq), .Q(flip_flop_3_q),
    .nQ(flip_flop_3_nq));
  flip_flop flip_flop_4 (
    .SRST(undriven), .ARST(undriven_2), .nCLK(flip_flop_3_q), .CLK(flip_flop_3_nq));  // open: Q, nQ
endmodule

module flip_flop (
  input  SRST,
  input  ARST,
  input  nCLK,
  input  CLK,
  output Q,
  output nQ
);

  wire nand_1_out, nand_2_out, nand_3_out, nand_4_out, nand_5_out, nand_6_out;

  nand nand_1 (nand_1_out, nQ, SRST, ARST, nCLK);
  nand nand_2 (nand_2_out, nCLK, Q);
  nand nand_3 (nand_3_out, nand_1_out, nand_4_out);
  nand nand_4 (nand_4_out, nand_3_out, nand_2_out, ARST);
  nand nand_5 (nand_5_out, ARST, nand_3_out, CLK);
  nand nand_6 (nand_6_out, CLK, nand_4_out);
  nand nand_7 (Q, nand_5_out, nQ);
  nand nand_8 (nQ, Q, nand_6_out, ARST);
endmodule
